# Fritzing sketch SumoBotV1.1_wiring_diagram (saved by Fritzing 0.9.3b)

parts:
  J1 = Basic Servo
  J2 = Basic Servo
  Part1 = Arduino Uno (Rev3)  # not connected
  Part2 = Arduino Prototyping Shield
  hc-sr1 = hc-sr04
  J3 = Infrared Proximity Sensor
  J4 = Infrared Proximity Sensor
  U2 = V_REG_MIC2920 [package=sot223]
  VCC3 = 4 x AAA Battery Mount

nets:
  GND: J1.gnd, J2.gnd, Part2.GND, hc-sr1.GND, J3.GND, J4.GND, U2.OUT
  N1: J1.vcc, Part2.N$428
  N2: J1.pulse, Part2.D10
  N3: J2.vcc, Part2.N$406
  N4: J2.pulse, Part2.D9
  N5: Part2.A0, J3.Vout
  N6: Part2.A1, J4.Vout
  N7: Part2.D12, hc-sr1.Trig
  N8: Part2.D13, hc-sr1.Echo
  VCC: Part2.+5V, hc-sr1.VCC, J3.Vcc, J4.Vcc
  N9: Part2.N$424, VCC3.+
